// Logisim project cpu.circ as structural Verilog: 7 circuits, main circuit main
module main (
  input  [31:0] INSTRUCTION,
  input  CLOCK,
  output [31:0] FETCH_ADDRESS,
  output [31:0] s0_Value,
  output [31:0] s1_Value,
  output [31:0] s2_Value,
  output [31:0] ra_Value,
  output [31:0] sp_Value,
  output [31:0] HI_Value,
  output [31:0] LO_Value
);

  Register #(.width(32)) PC ();  // open: D, en, Q, clk, clr
  Register #(.width(32)) LO ();  // open: D, en, Q, clk, clr
  Register #(.width(32)) HI ();  // open: D, en, Q, clk, clr

  // Other names for the same wires on the sheet: clk = CLOCK; fetch_addr[31:0] = FETCH_ADDRESS

  // Notes on the sheet:
  //   Output
  //   Inputs
endmodule

module MIPS (
  input  clk,
  input  RegWe,
  input  [3:0] ALUOp,
  input  ALUSrc,
  input  RegDst,
  input  ExtOp,
  output [31:0] s0,
  output [31:0] s1,
  output [31:0] s2,
  output [31:0] ra
);

  wire clock_1_out;
  wire [4:0] multiplexer_1_out, rd, rs, rt, sham;
  wire [5:0] functy, op;
  wire [15:0] imm16;
  wire [25:0] imm26;
  wire [31:0] alu_1_result, bit_extender_1_out, bit_extender_2_out, ifu_1_instruction, main_1_reg1,
       main_1_reg2_2, multiplexer_2_out, multiplexer_3_out;

  Clock clock_1 (.out(clock_1_out));
  IFU ifu_1 (.clk(clock_1_out), .instruction(ifu_1_instruction));
  Multiplexer #(.width(5), .enable("false")) multiplexer_1 (.in0(rt), .in1(rd), .out(multiplexer_1_out), .sel(RegDst));
  Decoder decoder_1 (
    .instruction(ifu_1_instruction), .op(op), .rs(rs), .rt(rt), .rd(rd), .sham(sham), .funct(functy),
    .imm16(imm16), .imm26(imm26));
  regfile_main main_1 (
    .Reg1_num(rs), .Reg2(rt), .Write_Reg_num(multiplexer_1_out), .Din(alu_1_result), .Write_Enable(RegWe),
    .Clock(clock_1_out), .Reg1(main_1_reg1), .Reg2_2(main_1_reg2_2), .s0_Value(s0), .s1_Value(s1),
    .s2_Value(s2), .ra_Value(ra));
  assign bit_extender_1_out = {{16{1'b0}}, imm16};  // Bit_Extender bit_extender_1
  assign bit_extender_2_out = {{16{imm16[15]}}, imm16};  // Bit_Extender bit_extender_2
  Multiplexer #(.width(32), .enable("false")) multiplexer_2 (
    .in0(bit_extender_1_out), .in1(bit_extender_2_out), .out(multiplexer_2_out), .sel(ExtOp));
  // Probe on op
  // Probe on rs
  // Probe on rt
  // Probe on rd
  // Probe on sham
  // Probe on functy
  // Probe on imm16
  // Probe on imm26
  Multiplexer #(.width(32), .enable("false")) multiplexer_3 (
    .in0(main_1_reg2_2), .in1(multiplexer_2_out), .out(multiplexer_3_out), .sel(ALUSrc));
  // Probe on op
  // Probe on rs
  // Probe on rt
  // Probe on rd
  // Probe on sham
  // Probe on functy
  // Probe on imm16
  // Probe on imm26
  ALU alu_1 (
    .AluOP(ALUOp), .X(main_1_reg1), .Result(alu_1_result), .Y(multiplexer_3_out));  // open: Equal, Signed_Overflow, Result_2
  // Probe on op
  // Probe on rs
  // Probe on rt
  // Probe on rd
  // Probe on sham
  // Probe on functy
  // Probe on imm16
  // Probe on imm26
endmodule

module IFU (
  input  clk,
  output [31:0] instruction
);

  wire [31:0] adder_1_out, PC_q;

  Register #(.width(32)) PC (.D(adder_1_out), .en(1'b1), .Q(PC_q), .clk(clk), .clr(1'b0));
  Adder #(.width(32)) adder_1 (.a(32'h4), .b(PC_q), .out(adder_1_out), .cin(1'b0));  // open: cout
  ROM #(.addrWidth(10), .dataWidth(32)) rom_1 (.addr(PC_q[11:2]), .data(instruction), .sel(1'b1));

  // Notes on the sheet:
  //   /4:word => byte
  //   contents of rom_1 (hex, n*v repeats v):
  //   22510020 26310020 2328020
endmodule

module Decoder (
  input  [31:0] instruction,
  output [25:0] imm26,
  output [15:0] imm16,
  output [5:0] op,
  output [4:0] rs,
  output [4:0] rt,
  output [4:0] rd,
  output [4:0] sham,
  output [5:0] funct
);


  assign funct = instruction[5:0];
  assign imm16 = instruction[15:0];
  assign imm26 = instruction[25:0];
  assign op = instruction[31:26];
  assign rd = instruction[15:11];
  assign rs = instruction[25:21];
  assign rt = instruction[20:16];
  assign sham = instruction[10:6];

  // Notes on the sheet:
  //   R 型指令译码
  //   I 型指令译码
  //   J 型指令译码
endmodule

module RAM (
  input  [31:0] Address,
  input  [31:0] Write_Data,
  input  Write_En,
  input  Clock,
  output [31:0] Read_Data
);

  RAM_part #(.addrWidth(24), .dataWidth(32), .bus("separate")) ram_1 (
    .addr(Address[25:2]), .din(Write_Data), .data(Read_Data), .str(Write_En), .sel(1'b1), .clk(Clock),
    .ld(1'b1), .clr(1'b0));
endmodule

module ControlUnit (
  input  add,
  input  addi,
  input  addiu,
  output RType,
  output RegWe,
  output [3:0] ALUOp,
  output ALUSrc,
  output RegDst,
  output ExtOp
);
endmodule

module InstructionTyper (
  input  [5:0] op,
  input  [5:0] funct,
  output RType,
  output RegWe,
  output [3:0] ALUOp,
  output ALUSrc,
  output RegDst,
  output ExtOp
);

  Comparator #(.width(6), .mode("unsigned")) comparator_1 (.a(op), .b({6{1'b0}}), .eq(RType));  // open: gt, lt
endmodule
